// Logisim project 8wproblem1.circ as structural Verilog
module main (
  input  in_1,
  input  in_2,
  input  in_3,
  input  in_4,
  output out_5,
  output out_6
);

  problem1 problem1_1 (.a(in_1), .b(in_2), .c(in_3), .d(in_4), .out1(out_5), .out2(out_6));
endmodule

// VHDL entity problem1, as the project stores it:
library ieee;
use ieee.std_logic_1164.all;

entity problem1 is
    port (
        a, b, c, d : in std_logic;
        out1 : out std_logic;
        out2 : out std_logic
    );
end entity problem1;

architecture bhv of problem1 is
begin
    out1 <= a and b and c and d;
    out2 <= a or b or c or d;
end architecture bhv;
