// Logisim project 8wproblem3.circ as structural Verilog
module main (
  input  in_1,
  input  [3:0] in_2
);

  wire [7:0] problem3_7seg_1_display;

  problem3_7seg problem3_7seg_1 (.en(in_1), .dat(in_2), .display(problem3_7seg_1_display));
  _7_Segment_Display u_7_segment_display_1 (
    .g(problem3_7seg_1_display[1]), .f(problem3_7seg_1_display[2]), .a(problem3_7seg_1_display[7]),
    .b(problem3_7seg_1_display[6]), .e(problem3_7seg_1_display[3]), .d(problem3_7seg_1_display[4]),
    .c(problem3_7seg_1_display[5]), .dp(problem3_7seg_1_display[0]));
endmodule

// VHDL entity problem3_7seg, as the project stores it:
library ieee;
use ieee.std_logic_1164.all;

entity problem3_7seg is
    port (
        en      : in std_logic;
        dat     : in std_logic_vector(3 downto 0);
        display : out std_logic_vector(7 downto 0)
    );
end entity problem3_7seg;

architecture bhv of problem3_7seg is
begin
    process(en, dat)
    begin
        if en = '0' then
            display <= "00000000";
        else
            case dat is
                when "0000" => display <= "11111010"; -- a
                when "0001" => display <= "00111110"; -- b
                when "0010" => display <= "00011010"; -- c
                when "0011" => display <= "01111010"; -- d
                when "0100" => display <= "10001110"; -- f
                when "0101" => display <= "11110110"; -- g
                when others => display <= "00000000";
            end case;
        end if;
    end process;
end architecture bhv;
