// Logisim project 8wproblem5.circ as structural Verilog
module main (
  input  [12:0] in_1,
  input  in_2
);

  wire [7:0] problem5_7seg_1_display;

  problem5_7seg problem5_7seg_1 (.vt(in_1), .en(in_2), .display(problem5_7seg_1_display));
  _7_Segment_Display u_7_segment_display_1 (
    .g(problem5_7seg_1_display[1]), .f(problem5_7seg_1_display[2]), .a(problem5_7seg_1_display[7]),
    .b(problem5_7seg_1_display[6]), .e(problem5_7seg_1_display[3]), .d(problem5_7seg_1_display[4]),
    .c(problem5_7seg_1_display[5]), .dp(problem5_7seg_1_display[0]));
endmodule

// VHDL entity problem5_7seg, as the project stores it:
library ieee;
use ieee.std_logic_1164.all;

entity problem5_7seg is
    port (
        vt      : in std_logic_vector(12 downto 0);
        en      : in std_logic;
        display : out std_logic_vector(7 downto 0)
    );
end entity problem5_7seg;

architecture bhv of problem5_7seg is
begin
    process(vt, en)
        variable count_ones : integer range 0 to 15;
    begin
        count_ones := 0;

        for i in vt'range loop
            if vt(i) = '1' then
                count_ones := count_ones + 1;
            end if;
        end loop;

        if en = '0' then
            display <= "00000000";
        else
            -- Bit order: a b c d e f g dp
            case count_ones is
                when  0 => display <= "11111100"; -- 0
                when  1 => display <= "01100000"; -- 1
                when  2 => display <= "11011010"; -- 2
                when  3 => display <= "11110010"; -- 3
                when  4 => display <= "01100110"; -- 4
                when  5 => display <= "10110110"; -- 5
                when  6 => display <= "10111110"; -- 6
                when  7 => display <= "11100000"; -- 7
                when  8 => display <= "11111110"; -- 8
                when  9 => display <= "11110110"; -- 9
                when 10 => display <= "11101110"; -- A
                when 11 => display <= "00111110"; -- b
                when 12 => display <= "10011100"; -- C
                when 13 => display <= "01111010"; -- d
                when 14 => display <= "10011110"; -- E
                when 15 => display <= "10001110"; -- F
                when others => display <= "00000000";
            end case;
        end if;
    end process;
end architecture bhv;
